// Logisim project zaehlwuerfel.circ as structural Verilog: 3 circuits, main circuit main
module main (
);

  wire and_1_out, and_2_out, and_3_out, and_4_out, button_1_out, not_1_out, not_2_out, or_1_out;
  wire [3:0] counter_1_q;

  Button button_1 (.out(button_1_out));
  Counter #(.max('hf), .width(4)) counter_1 (
    .count(1'b1), .Q(counter_1_q), .clk(button_1_out), .clr(and_1_out));  // open: load, D, carry, up
  and and_1 (and_1_out, counter_1_q[2], counter_1_q[1]);
  or or_1 (or_1_out, counter_1_q[2], and_2_out);
  and and_2 (and_2_out, counter_1_q[0], counter_1_q[1]);
  and and_3 (and_3_out, ~counter_1_q[0], ~counter_1_q[1], ~counter_1_q[2]);  // AND_Gate
  not not_1 (not_1_out, or_1_out);
  and and_4 (and_4_out, counter_1_q[2], counter_1_q[0]);
  not not_2 (not_2_out, and_4_out);
  anzeige anzeige_1 (.D(counter_1_q[0]), .C(and_3_out), .B(not_1_out), .A(not_2_out));
  // also tied to GND on the sheet: counter_1_q[3]
endmodule

module anzeige (
  input  D,
  input  C,
  input  B,
  input  A
);

  wire not_1_out, not_2_out, not_3_out, not_4_out;

  LED led_1 (.in(not_3_out));
  LED led_2 (.in(not_4_out));
  LED led_3 (.in(not_2_out));
  not not_1 (not_1_out, D);
  LED led_4 (.in(not_2_out));
  LED led_5 (.in(not_1_out));
  LED led_6 (.in(not_4_out));
  LED led_7 (.in(not_3_out));
  not not_2 (not_2_out, C);
  not not_3 (not_3_out, B);
  not not_4 (not_4_out, A);
endmodule

module main2 (
);

  wire and_1_out, and_2_out, and_3_out, button_1_out, nor_1_out, nor_2_out, nor_3_out;
  wire [3:0] counter_1_q;

  Button button_1 (.out(button_1_out));
  Counter #(.max('hf), .width(4)) counter_1 (
    .count(1'b1), .Q(counter_1_q), .clk(button_1_out), .clr(and_3_out));  // open: load, D, carry, up
  and and_1 (and_1_out, counter_1_q[0], counter_1_q[1]);
  and and_2 (and_2_out, counter_1_q[2], counter_1_q[0]);
  and and_3 (and_3_out, counter_1_q[1], counter_1_q[2]);
  nor nor_1 (nor_1_out, counter_1_q[2], counter_1_q[1], counter_1_q[0]);
  nor nor_2 (nor_2_out, and_1_out, 1'b0, counter_1_q[2]);
  nor nor_3 (nor_3_out, and_2_out, 1'b0, 1'b0);
  anzeige anzeige_1 (.D(counter_1_q[0]), .C(nor_1_out), .B(nor_2_out), .A(nor_3_out));
  // also tied to GND on the sheet: counter_1_q[3]

  // Notes on the sheet:
  //   x2
  //   x0
  //   x1
  //   74LS09
  //   74LS09
  //   74LS09
  //   74LS27
  //   74LS27
  //   74LS27
  //   Counter Reset
endmodule
